// Logisim project 4 Bit Multiplier using Adders.circ as structural Verilog: 2 circuits, main circuit main
module main (
  input  in_1,
  input  in_2,
  input  in_3,
  output out_4,
  output out_5
);

  wire and_1_out, and_2_out, xor_1_out;

  xor xor_1 (xor_1_out, in_1, in_2);
  xor xor_2 (out_4, xor_1_out, in_3);
  and and_1 (and_1_out, in_3, xor_1_out);
  and and_2 (and_2_out, in_2, in_1);
  or or_1 (out_5, and_1_out, and_2_out);
endmodule

module Multiplier (
  input  [3:0] in_1,
  input  [3:0] in_2,
  output [7:0] out_3
);

  wire and_2_out, and_3_out, and_4_out, and_5_out, and_6_out, and_7_out, and_8_out, and_9_out, and_10_out,
       and_11_out, and_12_out, and_13_out, and_14_out, and_15_out, and_16_out, main_1_out_5, main_2_out_4,
       main_2_out_5, main_3_out_4, main_3_out_5, main_4_out_4, main_4_out_5, main_5_out_5, main_6_out_4,
       main_6_out_5, main_7_out_4, main_7_out_5, main_8_out_4, main_8_out_5, main_9_out_5, main_10_out_5,
       main_11_out_5;

  and and_1 (out_3[0], in_1[0], in_2[0]);
  and and_2 (and_2_out, in_1[1], in_2[0]);
  main main_1 (.in_1(and_2_out), .in_2(and_5_out), .in_3(1'b0), .out_4(out_3[1]), .out_5(main_1_out_5));
  and and_3 (and_3_out, in_1[2], in_2[0]);
  and and_4 (and_4_out, in_1[3], in_2[0]);
  main main_2 (.in_1(and_3_out), .in_2(and_6_out), .in_3(main_1_out_5), .out_4(main_2_out_4), .out_5(main_2_out_5));
  main main_3 (.in_1(and_4_out), .in_2(and_7_out), .in_3(main_2_out_5), .out_4(main_3_out_4), .out_5(main_3_out_5));
  main main_4 (.in_1(1'b0), .in_2(and_8_out), .in_3(main_3_out_5), .out_4(main_4_out_4), .out_5(main_4_out_5));
  and and_5 (and_5_out, in_1[0], in_2[1]);
  and and_6 (and_6_out, in_1[1], in_2[1]);
  and and_7 (and_7_out, in_1[2], in_2[1]);
  and and_8 (and_8_out, in_1[3], in_2[1]);
  and and_9 (and_9_out, in_1[0], in_2[2]);
  main main_5 (.in_1(main_2_out_4), .in_2(and_9_out), .in_3(1'b0), .out_4(out_3[2]), .out_5(main_5_out_5));
  and and_10 (and_10_out, in_1[1], in_2[2]);
  main main_6 (.in_1(main_3_out_4), .in_2(and_10_out), .in_3(main_5_out_5), .out_4(main_6_out_4), .out_5(main_6_out_5));
  and and_11 (and_11_out, in_1[2], in_2[2]);
  main main_7 (.in_1(main_4_out_4), .in_2(and_11_out), .in_3(main_6_out_5), .out_4(main_7_out_4), .out_5(main_7_out_5));
  and and_12 (and_12_out, in_1[3], in_2[2]);
  main main_8 (.in_1(main_4_out_5), .in_2(and_12_out), .in_3(main_7_out_5), .out_4(main_8_out_4), .out_5(main_8_out_5));
  and and_13 (and_13_out, in_1[0], in_2[3]);
  main main_9 (.in_1(main_6_out_4), .in_2(and_13_out), .in_3(1'b0), .out_4(out_3[3]), .out_5(main_9_out_5));
  and and_14 (and_14_out, in_1[2], in_2[3]);
  and and_15 (and_15_out, in_1[1], in_2[3]);
  main main_10 (.in_1(main_7_out_4), .in_2(and_15_out), .in_3(main_9_out_5), .out_4(out_3[4]), .out_5(main_10_out_5));
  and and_16 (and_16_out, in_1[3], in_2[3]);
  main main_11 (.in_1(main_8_out_4), .in_2(and_14_out), .in_3(main_10_out_5), .out_4(out_3[5]), .out_5(main_11_out_5));
  main main_12 (.in_1(main_8_out_5), .in_2(and_16_out), .in_3(main_11_out_5), .out_4(out_3[6]), .out_5(out_3[7]));

  // Notes on the sheet:
  //   x00
  //   c10
  //   x10
  //   c11
  //   x30
  //   x20
  //   s12
  //   c12
  //   s13
  //   c13
  //   x01
  //   s14
  //   x11
  //   x21
  //   x31
  //   C20
  //   x02
  //   C21
  //   P2
  //   x12
  //   S23
  //   C22
  //   x22
  //   S24
  //   c23
  //   x32
  //   s25
  //   c30
  //   X03
  //   p3
  //   c31
  //   X13
  //   p4
  //   X23
  //   c32
  //   p5
  //   X33
  //   p6
  //   p7
endmodule
